# Fritzing sketch 433 (saved by Fritzing 0.6.3b)
breadboards: 1

parts:
  Arduino1 = Arduino
  Arduino2 = Arduino Mega
  U3 = Mystery_Part___4_pins
  U4 = Mystery_Part___3_pins

nets:
  N1: Arduino1.D12, U4.connector2
  N2: Arduino1.+5V, U4.connector1
  N3: Arduino1.GND, U4.connector0
  N4: Arduino2.+5V, U3.connector0
  N5: Arduino2.GND, U3.connector3
  N6: Arduino2.D47, U3.connector1
